# Fritzing sketch TSFRL_master_module (saved by Fritzing 0.9.0b)

parts:
  IC1 = Voltage Regulator [package=to220-igo]
  U1 = MAX485 [package=dil08]
  C1 = Capacitor Polarized [package=cpol-radial-100uf-25v]
  C2 = Capacitor Polarized [package=cpol-radial-10uf-25v]
  R1 = Resistor [tolerance=±5% resistance=220 package=THT]
  POWER = LED - 3mm [color="Red (633nm)" package="3 mm [THT]"]
  J1 = rounded female pin header, 8 pins [form="♀ (female rounded)"]
  IC2 = Hex Inverter Schmitt Trigger SN74HC14 [package="DIP (Dual Inline)"]
  J2 = male pin header, 5 pins [form="♂ (male)"]
  TEST = LED - 3mm [color="Blue (525nm)" current=20pA package="3 mm [THT]"]
  DATA = LED - 3mm [color="Yellow (595nm)" package="3 mm [THT]"]
  ERR = LED - 3mm [color="Red (633nm)" package="3 mm [THT]"]
  DONE = LED - 3mm [color="Green (570nm)" package="3 mm [THT]"]
  Part1 = Arduino Nano (Rev3.0)

nets:
  GND: IC1.GND, U1.GND, C1.-, C2.-, POWER.cathode, J1.pin1, IC2.GND, TEST.cathode, DATA.cathode, Part1.GND
  12V: IC1.IN, C1.+
  N1: IC1.OUT, C2.+, R1.Pin_0
  5V: R1.Pin_1, POWER.anode, J1.pin8, IC2.VCC, Part1.5V
  N2: J1.pin2, J2.pin5, Part1.RESET
  N3: J1.pin3, IC2.3A
  N4: J1.pin4, IC2.2A
  N5: J1.pin5, IC2.1A
  N6: J1.pin6, IC2.4A
  N7: J1.pin7, IC2.5A
  N8: IC2.1Y, Part1.D5
  N9: IC2.2Y, Part1.D4
  N10: IC2.3Y, Part1.D3
  N11: IC2.4Y, Part1.D6
  N12: IC2.5Y, Part1.D7
  N13: TEST.anode, Part1.D8
  N14: DATA.anode, Part1.D13/SCK
  N15: ERR.anode, Part1.D10
  N16: DONE.anode, Part1.D9

notes:
  TSFRL_master_module_keys
  8) +5v
  7) keyUP
  6) keyRIGHT
  5) keyLEFT
  4) keyDOWN
  3)keySTART
  2)keySTOP/CANCEL
  1)GND
